// Logisim project TrafficLight.circ as structural Verilog: 4 circuits, main circuit main
module main (
  input  Set_to_1,
  output out_2
);

  wire and_1_out, and_3_out, clock_1_out, GREEN, half_adder_1_s, half_adder_2_c, half_adder_2_s,
       half_adder_3_c, half_adder_3_s, half_adder_4_c, half_adder_4_s, half_adder_5_c, half_adder_5_s,
       half_adder_6_c, half_adder_6_s, half_adder_7_c, half_adder_7_s, n7_bit_comparator_2_out_5,
       n7_bit_comparator_3_out_5, n7_bit_comparator_4_out_5, RED, RESET, YELLOW;
  wire [6:0] Number;

  Half_Adder half_adder_1 (.A(Number[6]), .B(half_adder_2_c), .S(half_adder_1_s), .C(out_2));
  D_Flip_Flop d_ff_1 (.clk(clock_1_out), .D(half_adder_1_s), .Q(Number[6]), .reset(RESET));  // open: Qn, preset, en
  Half_Adder half_adder_2 (.A(Number[5]), .B(half_adder_3_c), .S(half_adder_2_s), .C(half_adder_2_c));
  D_Flip_Flop d_ff_2 (.clk(clock_1_out), .D(half_adder_2_s), .Q(Number[5]), .reset(RESET));  // open: Qn, preset, en
  _7_bit_comparator u_7_bit_comparator_1 (.A(Number), .B(7'b0100011), .out_5(GREEN));  // open: out_3, out_4
  _7_bit_comparator u_7_bit_comparator_2 (
    .A(Number), .B(7'b0101110), .out_5(n7_bit_comparator_2_out_5));  // open: out_3, out_4
  _7_bit_comparator u_7_bit_comparator_3 (
    .A(Number), .B(7'b1000100), .out_5(n7_bit_comparator_3_out_5));  // open: out_3, out_4
  _7_bit_comparator u_7_bit_comparator_4 (
    .A(Number), .B(7'b1001111), .out_5(n7_bit_comparator_4_out_5), .out_4(RESET));  // open: out_3
  Half_Adder half_adder_3 (.A(Number[4]), .B(half_adder_4_c), .S(half_adder_3_s), .C(half_adder_3_c));
  D_Flip_Flop d_ff_3 (.clk(clock_1_out), .D(half_adder_3_s), .Q(Number[4]), .reset(RESET));  // open: Qn, preset, en
  and and_1 (and_1_out, ~GREEN, n7_bit_comparator_2_out_5);  // AND_Gate
  and and_2 (RED, ~n7_bit_comparator_2_out_5, n7_bit_comparator_3_out_5);  // AND_Gate
  and and_3 (and_3_out, ~n7_bit_comparator_3_out_5, n7_bit_comparator_4_out_5);  // AND_Gate
  Half_Adder half_adder_4 (.A(Number[3]), .B(half_adder_6_c), .S(half_adder_4_s), .C(half_adder_4_c));
  D_Flip_Flop d_ff_4 (.clk(clock_1_out), .D(half_adder_4_s), .Q(Number[3]), .reset(RESET));  // open: Qn, preset, en
  or or_1 (YELLOW, and_1_out, and_3_out);
  Half_Adder half_adder_5 (.A(Number[1]), .B(half_adder_7_c), .S(half_adder_5_s), .C(half_adder_5_c));
  Half_Adder half_adder_6 (.A(Number[2]), .B(half_adder_5_c), .S(half_adder_6_s), .C(half_adder_6_c));
  D_Flip_Flop d_ff_5 (.clk(clock_1_out), .D(half_adder_6_s), .Q(Number[2]), .reset(RESET));  // open: Qn, preset, en
  Half_Adder half_adder_7 (.A(Number[0]), .B(Set_to_1), .S(half_adder_7_s), .C(half_adder_7_c));
  D_Flip_Flop d_ff_6 (.clk(clock_1_out), .D(half_adder_5_s), .Q(Number[1]), .reset(RESET));  // open: Qn, preset, en
  Clock clock_1 (.out(clock_1_out));
  D_Flip_Flop d_ff_7 (.clk(clock_1_out), .D(half_adder_7_s), .Q(Number[0]), .reset(RESET));  // open: Qn, preset, en
  LED led_1 (.in(RED));
  LED led_2 (.in(YELLOW));
  LED led_3 (.in(GREEN));

  // Notes on the sheet:
  //   35
  //   46
  //   68
  //   79
  //   ← Start Clock
  //   Y = 11 
  //   R = 22
  //   Birth date: 22/11/2000
  //   G = 34 ID =000004634
endmodule

// H+
module Half_Adder (
  input  A,
  input  B,
  output S,
  output C
);

  xor xor_1 (S, A, B);
  and and_1 (C, A, B);
endmodule

module _4_bit_Comparator (
  input  [3:0] A,
  input  [3:0] B,
  output out_3,
  output out_4,
  output out_5
);

  wire _0, _1, _2, _3, and_2_out, and_3_out, and_4_out, and_5_out;

  xnor xnor_1 (_0, A[0], B[0]);
  xnor xnor_2 (_1, A[1], B[1]);
  xnor xnor_3 (_2, A[2], B[2]);
  and and_1 (out_4, _0, _1, _2, _3);
  xnor xnor_4 (_3, A[3], B[3]);
  nor nor_1 (out_5, out_4, out_3);
  and and_2 (and_2_out, A[0], _1, _3, _2, ~B[0]);  // AND_Gate
  and and_3 (and_3_out, A[1], _3, _2, ~B[1]);  // AND_Gate
  and and_4 (and_4_out, A[2], _3, ~B[2]);  // AND_Gate
  and and_5 (and_5_out, A[3], ~B[3]);  // AND_Gate
  or or_1 (out_3, and_2_out, and_3_out, and_4_out, and_5_out);

  // Other names for the same wires on the sheet: tunnel = out_4; tunnel_t = out_3

  // Notes on the sheet:
  //   INPUT
  //   EQUIVALENCE
  //   A    B
  //   OUTPUT
  //   A > B
endmodule

module _7_bit_comparator (
  input  [6:0] A,
  input  [6:0] B,
  output out_3,
  output out_4,
  output out_5
);

  wire and_1_out, n4_bit_comparator_1_out_3, n4_bit_comparator_1_out_4, n4_bit_comparator_2_out_3,
       n4_bit_comparator_2_out_4;

  _4_bit_Comparator u_4_bit_comparator_1 (
    .out_3(n4_bit_comparator_1_out_3), .out_4(n4_bit_comparator_1_out_4), .A(A[3:0]), .B(B[3:0]));  // open: out_5
  _4_bit_Comparator u_4_bit_comparator_2 (
    .out_3(n4_bit_comparator_2_out_3), .out_4(n4_bit_comparator_2_out_4), .A({1'b0, A[6:4]}),
    .B({1'b0, B[6:4]}));  // open: out_5
  and and_1 (and_1_out, n4_bit_comparator_1_out_3, n4_bit_comparator_2_out_4);
  or or_1 (out_3, and_1_out, n4_bit_comparator_2_out_3);
  nor nor_1 (out_5, out_4, out_3);
  and and_2 (out_4, n4_bit_comparator_1_out_4, n4_bit_comparator_2_out_4);

  // Other names for the same wires on the sheet: A_4_0[3:0] = A[3:0]; A_8_4[2:0] = A[6:4]; B_4_0[3:0] = B[3:0];
  //   B_8_4[2:0] = B[6:4]; tunnel = out_4; tunnel_t = out_3

  // Notes on the sheet:
  //   INPUT
  //   Cascading Comparator Cicuit
  //   OUTPUT
endmodule
