// Logisim project Lock.circ as structural Verilog: 5 circuits, main circuit main
module main (
);

  wire and_1_out, and_2_out, clock_1_out, CLR, Clr_out, d_ff_1_qn, d_ff_2_qn, d_ff_3_qn, d_ff_4_qn,
       d_ff_5_qn, d_ff_6_q, d_ff_6_qn, K0, K0_out, K1, K1_out, K2, K2_out, K3, K3_out, S0, S1, S2, S3,
       s_0_logic_1_out_9, s_1_logic_1_out_9, s_2_logic_1_out_9, s_3_logic_1_out_9, SUBMIT_out;

  Button u_K3 (.out(K3_out));
  Button u_K2 (.out(K2_out));
  D_Flip_Flop d_ff_1 (.clk(K3_out), .D(d_ff_1_qn), .Q(K3), .Qn(d_ff_1_qn), .reset(CLR));  // open: preset, en
  Button u_K1 (.out(K1_out));
  D_Flip_Flop d_ff_2 (.clk(K2_out), .D(d_ff_2_qn), .Q(K2), .Qn(d_ff_2_qn), .reset(CLR));  // open: preset, en
  Button u_K0 (.out(K0_out));
  D_Flip_Flop d_ff_3 (.clk(K1_out), .D(d_ff_3_qn), .Q(K1), .Qn(d_ff_3_qn), .reset(CLR));  // open: preset, en
  Button u_Clr (.out(Clr_out));
  D_Flip_Flop d_ff_4 (.clk(K0_out), .D(d_ff_4_qn), .Q(K0), .Qn(d_ff_4_qn), .reset(CLR));  // open: preset, en
  S_3_logic s_3_logic_1 (
    .out_9(s_3_logic_1_out_9), .S2(S2), .S1(S1), .S0(S0), .S3(S3), .K3(K3), .K2(K2), .K1(K1), .K0(K0));
  S_2_logic s_2_logic_1 (
    .out_9(s_2_logic_1_out_9), .S3(S3), .S2(S2), .S1(S1), .S0(S0), .K3(K3), .K2(K2), .K1(K1), .K0(K0));
  S_1_logic s_1_logic_1 (
    .K3(K3), .K2(K2), .K1(K1), .K0(K0), .out_9(s_1_logic_1_out_9), .S3(S3), .S2(S2), .S1(S1), .S0(S0));
  S_0_logic s_0_logic_1 (
    .K3(K3), .K2(K2), .K1(K1), .K0(K0), .out_9(s_0_logic_1_out_9), .S3(S3), .S2(S2), .S1(S1), .S0(S0));
  D_Flip_Flop d_ff_5 (.clk(Clr_out), .D(d_ff_5_qn), .Q(CLR), .Qn(d_ff_5_qn), .reset(CLR));  // open: preset, en
  Register #(.width(1)) R3 (.D(s_3_logic_1_out_9), .Q(S3), .clk(and_1_out), .clr(CLR));  // open: en
  Register #(.width(1)) R2 (.D(s_2_logic_1_out_9), .Q(S2), .clk(and_1_out), .clr(CLR));  // open: en
  Register #(.width(1)) R1 (.D(s_1_logic_1_out_9), .Q(S1), .clk(and_1_out), .clr(CLR));  // open: en
  Register #(.width(1)) R0 (.D(s_0_logic_1_out_9), .Q(S0), .clk(and_1_out), .clr(CLR));  // open: en
  Button SUBMIT (.out(SUBMIT_out));
  D_Flip_Flop d_ff_6 (.clk(SUBMIT_out), .D(d_ff_6_qn), .Q(d_ff_6_q), .Qn(d_ff_6_qn), .reset(CLR));  // open: preset, en
  and and_1 (and_1_out, d_ff_6_q, clock_1_out);
  Clock clock_1 (.out(clock_1_out));
  LED led_1 (.in(and_2_out));
  and and_2 (and_2_out, S3, ~S2, ~S1, S0);  // AND_Gate

  // Notes on the sheet:
  //   STATE LOGIC
  //   INPUT LOGIC
  //   OUTPUT LOGIC
endmodule

// S'2
module S_2_logic (
  input  K3,
  input  K2,
  input  K1,
  input  K0,
  input  S3,
  input  S2,
  input  S1,
  input  S0,
  output out_9
);

  wire and_1_out, and_2_out, and_3_out;

  and and_1 (and_1_out, K3, K2);
  and and_2 (and_2_out, K2, ~K3);  // AND_Gate
  and and_3 (and_3_out, and_1_out, ~K1);  // AND_Gate
  Multiplexer #(.select(4), .enable("false")) multiplexer_1 (
    .in0(K3), .in1(and_2_out), .in2(1'b0), .in3(1'b0), .in4(1'b0), .in5(and_1_out), .in6(and_3_out),
    .in7(1'b0), .in8(1'b0), .in9(1'b0), .in10(1'b0), .in11(1'b0), .in12(1'b0), .in13(1'b0), .in14(1'b0),
    .in15(1'b0), .out(out_9), .sel({S3, S2, S1, S0}));
endmodule

// S'1
module S_1_logic (
  input  K3,
  input  K2,
  input  K1,
  input  K0,
  input  S3,
  input  S2,
  input  S1,
  input  S0,
  output out_9
);

  wire and_1_out, and_2_out, and_3_out, and_4_out;

  and and_1 (and_1_out, ~K3, ~K2);  // AND_Gate
  and and_2 (and_2_out, K3, K2);
  and and_3 (and_3_out, and_1_out, K1);
  and and_4 (and_4_out, and_2_out, ~K1);  // AND_Gate
  Multiplexer #(.select(4), .disabled(0), .enable("false")) multiplexer_1 (
    .in0(1'b0), .in1(and_1_out), .in2(and_3_out), .in3(1'b0), .in4(1'b0), .in5(and_2_out), .in6(and_4_out),
    .in7(1'b0), .in8(1'b0), .in9(1'b0), .in10(1'b0), .in11(1'b0), .in12(1'b0), .in13(1'b0), .in14(1'b0),
    .in15(1'b0), .out(out_9), .sel({S3, S2, S1, S0}));
endmodule

// S'0
module S_0_logic (
  input  K3,
  input  K2,
  input  K1,
  input  K0,
  input  S3,
  input  S2,
  input  S1,
  input  S0,
  output out_9
);

  wire and_1_out, and_2_out, and_3_out, and_4_out, and_5_out, and_6_out;

  and and_1 (and_1_out, K3, K2);
  and and_2 (and_2_out, and_1_out, and_3_out);
  and and_3 (and_3_out, ~K1, ~K0);  // AND_Gate
  and and_4 (and_4_out, ~K3, ~K2, K1);  // AND_Gate
  and and_5 (and_5_out, and_4_out, K0);
  and and_6 (and_6_out, ~K3, K2, K1);  // AND_Gate
  Multiplexer #(.select(4), .disabled(0), .enable("false")) multiplexer_1 (
    .in0(1'b1), .in1(1'b0), .in2(and_4_out), .in3(and_5_out), .in4(and_6_out), .in5(1'b0), .in6(and_1_out),
    .in7(and_2_out), .in8(1'b0), .in9(1'b1), .in10(1'b0), .in11(1'b0), .in12(1'b0), .in13(1'b0), .in14(1'b0),
    .in15(1'b0), .out(out_9), .sel({S3, S2, S1, S0}));
endmodule

// S'3
module S_3_logic (
  input  K3,
  input  K2,
  input  K1,
  input  K0,
  input  S3,
  input  S2,
  input  S1,
  input  S0,
  output out_9
);

  wire and_1_out, and_2_out, and_3_out, and_4_out, and_5_out, and_6_out, and_7_out, and_8_out;

  and and_1 (and_1_out, ~K3, ~K2);  // AND_Gate
  and and_2 (and_2_out, K3, K2);
  and and_3 (and_3_out, and_1_out, ~K1);  // AND_Gate
  and and_4 (and_4_out, and_1_out, K1);
  and and_5 (and_5_out, K2, ~K3);  // AND_Gate
  and and_6 (and_6_out, K3, ~K2);  // AND_Gate
  and and_7 (and_7_out, and_2_out, K1);
  and and_8 (and_8_out, and_2_out, ~K1);  // AND_Gate
  Multiplexer #(.select(4), .enable("false")) multiplexer_1 (
    .in0(1'b0), .in1(1'b0), .in2(and_3_out), .in3(and_4_out), .in4(and_5_out), .in5(and_6_out),
    .in6(and_7_out), .in7(and_8_out), .in8(1'b1), .in9(1'b1), .in10(1'b0), .in11(1'b0), .in12(1'b0),
    .in13(1'b0), .in14(1'b0), .in15(1'b0), .out(out_9), .sel({S3, S2, S1, S0}));
endmodule
