// Logisim project Calculator.circ as structural Verilog: 12 circuits, main circuit main
module main (
);

  wire _0, _1, _2, _3, _4, _5, _6, _7, _8, _9, alu_1_sign, and_1_out, and_2_out, and_3_out, ans,
       Any_Operation, CE, CE_only, n5_digit_comparator_1_out_12, n5_digit_comparator_2_out_12,
       Number_Pressed, Operation, Operator, operator_bit_1_out_3, operator_bit_1_out_4, operator_bit_1_out_5,
       operator_bit_1_out_6, operator_bit_1_out_7, operator_bit_1_out_8, operator_bit_1_out_9,
       operator_bit_1_out_10, or_2_out, or_3_out, or_4_out, or_5_out, or_7_out, Sign, sign_bit_1_out_2,
       sign_bit_1_out_3, sign_bit_1_out_4, sign_bit_1_out_5, sign_bit_1_out_6, sign_bit_1_out_7,
       sign_bit_1_out_8, sign_bit_1_out_9, tunnel, tunnel_t, tunnel_t_t;
  wire [3:0] A1, A2, A3, A4, A5, B1, B2, B3, B4, B5, D1, D2, D3, D4, D5, priority_encoder_1_out, S1, S2, S3,
       S4, S5, S_prime_1, S_prime_2, S_prime_3, S_prime_4, S_prime_5;

  Priority_Encoder #(.select(4)) priority_encoder_1 (
    .in0(_0), .in1(_1), .in2(_2), .in3(_3), .in4(_4), .in5(_5), .in6(_6), .in7(_7), .in8(_8), .in9(_9),
    .out(priority_encoder_1_out));  // open: in10, in11, in12, in13, in14, in15
  or or_1 (Any_Operation, tunnel_t, tunnel);
  Register #(.width(4)) register_1 (
    .D(priority_encoder_1_out), .Q(A1), .clk(Number_Pressed), .clr(or_2_out));  // open: en
  Register #(.width(4)) register_2 (.D(A1), .Q(B1), .clk(Any_Operation), .clr(CE));  // open: en
  Register #(.width(4)) register_3 (.D(S1), .Q(S_prime_1), .clk(tunnel_t_t), .clr(CE_only));  // open: en
  Register #(.width(4)) register_4 (.D(A1), .Q(A2), .clk(Number_Pressed), .clr(or_2_out));  // open: en
  Register #(.width(4)) register_5 (.D(A2), .Q(B2), .clk(Any_Operation), .clr(CE));  // open: en
  Register #(.width(4)) register_6 (.D(S2), .Q(S_prime_2), .clk(tunnel_t_t), .clr(CE_only));  // open: en
  Twister twister_1 (.A(S_prime_5), .In(ans), .B(A5), .B_prime(D5));  // open: A_prime
  ALU alu_1 (
    .A5(B5), .A4(B4), .A3(B3), .A2(B2), .A1(B1), .B5(A5), .B4(A4), .B3(A3), .B2(A2), .B1(A1), .S5(S5),
    .S4(S4), .S3(S3), .S2(S2), .S1(S1), .Sign_of_A(Sign), .Sign_of_B(1'b0), .Sign(alu_1_sign),
    .Operation(Operator));
  Twister twister_2 (.A(S_prime_4), .In(ans), .B(A4), .B_prime(D4));  // open: A_prime
  _5_digit_Comparator u_5_digit_comparator_1 (
    .out_12(n5_digit_comparator_1_out_12), .A5(B5), .A4(B4), .A3(B3), .A2(B2), .A1(B1), .B5(4'b0000),
    .B4(4'b0000), .B3(4'b0000), .B2(4'b0000), .B1(4'b0000));  // open: out_13, out_11
  and and_1 (and_1_out, n5_digit_comparator_1_out_12, n5_digit_comparator_2_out_12);
  _5_digit_Comparator u_5_digit_comparator_2 (
    .out_12(n5_digit_comparator_2_out_12), .A5(4'b0000), .A4(4'b0000), .A3(4'b0000), .A2(4'b0000),
    .A1(4'b0000), .B5(A5), .B4(A4), .B3(A3), .B2(A2), .B1(A1));  // open: out_13, out_11
  Register #(.width(4)) register_7 (.D(A2), .Q(A3), .clk(Number_Pressed), .clr(or_2_out));  // open: en
  Register #(.width(4)) register_8 (.D(A3), .Q(B3), .clk(Any_Operation), .clr(CE));  // open: en
  Register #(.width(4)) register_9 (.D(S3), .Q(S_prime_3), .clk(tunnel_t_t), .clr(CE_only));  // open: en
  Twister twister_3 (.A(S_prime_3), .In(ans), .B(A3), .B_prime(D3));  // open: A_prime
  Register #(.width(4)) register_10 (.D(A3), .Q(A4), .clk(Number_Pressed), .clr(or_2_out));  // open: en
  Register #(.width(4)) register_11 (.D(A4), .Q(B4), .clk(Any_Operation), .clr(CE));  // open: en
  Register #(.width(4)) register_12 (.D(S4), .Q(S_prime_4), .clk(tunnel_t_t), .clr(CE_only));  // open: en
  Twister twister_4 (.A(S_prime_2), .In(ans), .B(A2), .B_prime(D2));  // open: A_prime
  and and_2 (and_2_out, and_1_out, tunnel_t);
  Register #(.width(4)) register_13 (.D(A4), .Q(A5), .clk(Number_Pressed), .clr(or_2_out));  // open: en
  or or_2 (or_2_out, CE, Any_Operation);
  Register #(.width(4)) register_14 (.D(A5), .Q(B5), .clk(Any_Operation), .clr(CE));  // open: en
  Register #(.width(4)) register_15 (.D(S5), .Q(S_prime_5), .clk(tunnel_t_t), .clr(CE_only));  // open: en
  or or_3 (or_3_out, tunnel_t_t, and_2_out);
  or or_4 (or_4_out, alu_1_sign, tunnel_t);
  or or_5 (or_5_out, and_3_out, CE_only);
  and and_3 (and_3_out, Number_Pressed, ans);
  Twister twister_5 (.A(S_prime_1), .In(ans), .B(A1), .B_prime(D1));  // open: A_prime
  D_Flip_Flop d_ff_1 (.clk(tunnel_t_t), .D(tunnel_t_t), .Q(ans), .reset(or_7_out));  // open: Qn, preset, en
  D_Flip_Flop d_ff_2 (.clk(Any_Operation), .D(Any_Operation), .Q(Operation), .reset(CE));  // open: Qn, preset, en
  D_Flip_Flop d_ff_3 (.clk(Any_Operation), .D(tunnel_t), .Q(Operator), .reset(CE));  // open: Qn, preset, en
  D_Flip_Flop d_ff_4 (.clk(or_3_out), .D(or_4_out), .Q(Sign), .reset(or_5_out));  // open: Qn, preset, en
  or or_6 (CE, tunnel_t_t, CE_only);
  or or_7 (or_7_out, Any_Operation, CE_only, Number_Pressed);
  _7_Segment_Display u_7_segment_display_1 (
    .g(sign_bit_1_out_2), .f(sign_bit_1_out_3), .a(sign_bit_1_out_4), .b(sign_bit_1_out_5),
    .e(sign_bit_1_out_6), .d(sign_bit_1_out_7), .c(sign_bit_1_out_8), .dp(sign_bit_1_out_9));
  Sign_Bit sign_bit_1 (
    .out_2(sign_bit_1_out_2), .out_3(sign_bit_1_out_3), .out_4(sign_bit_1_out_4), .out_5(sign_bit_1_out_5),
    .out_6(sign_bit_1_out_6), .out_7(sign_bit_1_out_7), .out_8(sign_bit_1_out_8), .out_9(sign_bit_1_out_9),
    .in_1(Sign));
  Hex_Digit_Display hex_digit_display_1 (.value(D5));  // open: dp
  Button u_CE (.out(CE_only));
  Button u__7 (.out(_7));
  Button u__4 (.out(_4));
  Button u__1 (.out(_1));
  Button u__0 (.out(_0));
  Hex_Digit_Display hex_digit_display_2 (.value(D4));  // open: dp
  Hex_Digit_Display hex_digit_display_3 (.value(D3));  // open: dp
  Button C ();  // open: out
  Button u__8 (.out(_8));
  Button u__5 (.out(_5));
  Button u__2 (.out(_2));
  Hex_Digit_Display hex_digit_display_4 (.value(D2));  // open: dp
  Hex_Digit_Display hex_digit_display_5 (.value(D1));  // open: dp
  Button button ();  // open: out
  Button u__9 (.out(_9));
  Button u__6 (.out(_6));
  Button u__3 (.out(_3));
  Button button_2 (.out(tunnel_t_t));
  _7_Segment_Display u_7_segment_display_2 (
    .g(operator_bit_1_out_3), .f(operator_bit_1_out_4), .a(operator_bit_1_out_5), .b(operator_bit_1_out_6),
    .e(operator_bit_1_out_7), .d(operator_bit_1_out_8), .c(operator_bit_1_out_9), .dp(operator_bit_1_out_10));
  Operator_Bit operator_bit_1 (
    .in_2(Operator), .EN(Operation), .out_3(operator_bit_1_out_3), .out_4(operator_bit_1_out_4),
    .out_5(operator_bit_1_out_5), .out_6(operator_bit_1_out_6), .out_7(operator_bit_1_out_7),
    .out_8(operator_bit_1_out_8), .out_9(operator_bit_1_out_9), .out_10(operator_bit_1_out_10));
  Button button_3 ();  // open: out
  Button button_4 (.out(tunnel_t));
  Button button_5 (.out(tunnel));
  Button x ();  // open: out
  Button button_6 ();  // open: out

  // Notes on the sheet:
  //   Registers - B
  //   Registers - A
  //   Registers - S
  //   Decides which array of registers to display
  //   Result on Display
  //   Ongoing Operation Bit
  //   Operator Bit
  //   Sign Bit
  //   @Sadig Akhund
endmodule

module test (
  input  [3:0] A5,
  input  [3:0] A4,
  input  [3:0] A3,
  input  [3:0] A2,
  input  [3:0] A1,
  input  [3:0] B5,
  input  [3:0] B4,
  input  [3:0] B3,
  input  [3:0] B2,
  input  [3:0] B1,
  input  Sign_of_A,
  input  Sign_of_B,
  input  Op
);

  wire alu_1_sign, operator_bit_1_out_3, operator_bit_1_out_4, operator_bit_1_out_5, operator_bit_1_out_6,
       operator_bit_1_out_7, operator_bit_1_out_8, operator_bit_1_out_9, operator_bit_1_out_10,
       sign_bit_1_out_2, sign_bit_1_out_3, sign_bit_1_out_4, sign_bit_1_out_5, sign_bit_1_out_6,
       sign_bit_1_out_7, sign_bit_1_out_8, sign_bit_1_out_9, sign_bit_2_out_2, sign_bit_2_out_3,
       sign_bit_2_out_4, sign_bit_2_out_5, sign_bit_2_out_6, sign_bit_2_out_7, sign_bit_2_out_8,
       sign_bit_2_out_9, sign_bit_3_out_2, sign_bit_3_out_3, sign_bit_3_out_4, sign_bit_3_out_5,
       sign_bit_3_out_6, sign_bit_3_out_7, sign_bit_3_out_8, sign_bit_3_out_9;
  wire [3:0] S1, S2, S3, S4, S5;

  ALU alu_1 (
    .A5(A5), .A4(A4), .A3(A3), .A2(A2), .A1(A1), .B5(B5), .B4(B4), .B3(B3), .B2(B2), .B1(B1), .S5(S5),
    .S4(S4), .S3(S3), .S2(S2), .S1(S1), .Sign_of_A(Sign_of_A), .Sign_of_B(Sign_of_B), .Sign(alu_1_sign),
    .Operation(Op));
  _7_Segment_Display u_7_segment_display_1 (
    .g(operator_bit_1_out_3), .f(operator_bit_1_out_4), .a(operator_bit_1_out_5), .b(operator_bit_1_out_6),
    .e(operator_bit_1_out_7), .d(operator_bit_1_out_8), .c(operator_bit_1_out_9), .dp(operator_bit_1_out_10));
  Operator_Bit operator_bit_1 (
    .in_2(Op), .EN(1'b1), .out_3(operator_bit_1_out_3), .out_4(operator_bit_1_out_4),
    .out_5(operator_bit_1_out_5), .out_6(operator_bit_1_out_6), .out_7(operator_bit_1_out_7),
    .out_8(operator_bit_1_out_8), .out_9(operator_bit_1_out_9), .out_10(operator_bit_1_out_10));
  _7_Segment_Display u_7_segment_display_2 (
    .g(sign_bit_1_out_2), .f(sign_bit_1_out_3), .a(sign_bit_1_out_4), .b(sign_bit_1_out_5),
    .e(sign_bit_1_out_6), .d(sign_bit_1_out_7), .c(sign_bit_1_out_8), .dp(sign_bit_1_out_9));
  Sign_Bit sign_bit_1 (
    .out_2(sign_bit_1_out_2), .out_3(sign_bit_1_out_3), .out_4(sign_bit_1_out_4), .out_5(sign_bit_1_out_5),
    .out_6(sign_bit_1_out_6), .out_7(sign_bit_1_out_7), .out_8(sign_bit_1_out_8), .out_9(sign_bit_1_out_9),
    .in_1(Sign_of_A));
  _7_Segment_Display u_7_segment_display_3 (
    .g(sign_bit_2_out_2), .f(sign_bit_2_out_3), .a(sign_bit_2_out_4), .b(sign_bit_2_out_5),
    .e(sign_bit_2_out_6), .d(sign_bit_2_out_7), .c(sign_bit_2_out_8), .dp(sign_bit_2_out_9));
  Sign_Bit sign_bit_2 (
    .out_2(sign_bit_2_out_2), .out_3(sign_bit_2_out_3), .out_4(sign_bit_2_out_4), .out_5(sign_bit_2_out_5),
    .out_6(sign_bit_2_out_6), .out_7(sign_bit_2_out_7), .out_8(sign_bit_2_out_8), .out_9(sign_bit_2_out_9),
    .in_1(Sign_of_B));
  _7_Segment_Display u_7_segment_display_4 (
    .g(sign_bit_3_out_2), .f(sign_bit_3_out_3), .a(sign_bit_3_out_4), .b(sign_bit_3_out_5),
    .e(sign_bit_3_out_6), .d(sign_bit_3_out_7), .c(sign_bit_3_out_8), .dp(sign_bit_3_out_9));
  Sign_Bit sign_bit_3 (
    .out_2(sign_bit_3_out_2), .out_3(sign_bit_3_out_3), .out_4(sign_bit_3_out_4), .out_5(sign_bit_3_out_5),
    .out_6(sign_bit_3_out_6), .out_7(sign_bit_3_out_7), .out_8(sign_bit_3_out_8), .out_9(sign_bit_3_out_9),
    .in_1(alu_1_sign));
  Hex_Digit_Display hex_digit_display_1 (.value(A4));  // open: dp
  Hex_Digit_Display hex_digit_display_2 (.value(A5));  // open: dp
  Hex_Digit_Display hex_digit_display_3 (.value(B5));  // open: dp
  Hex_Digit_Display hex_digit_display_4 (.value(B4));  // open: dp
  Hex_Digit_Display hex_digit_display_5 (.value(S4));  // open: dp
  Hex_Digit_Display hex_digit_display_6 (.value(S5));  // open: dp
  Hex_Digit_Display hex_digit_display_7 (.value(A3));  // open: dp
  Hex_Digit_Display hex_digit_display_8 (.value(A2));  // open: dp
  Hex_Digit_Display hex_digit_display_9 (.value(B2));  // open: dp
  Hex_Digit_Display hex_digit_display_10 (.value(B3));  // open: dp
  Hex_Digit_Display hex_digit_display_11 (.value(S2));  // open: dp
  Hex_Digit_Display hex_digit_display_12 (.value(S3));  // open: dp
  Hex_Digit_Display hex_digit_display_13 (.value(A1));  // open: dp
  Hex_Digit_Display hex_digit_display_14 (.value(B1));  // open: dp
  Hex_Digit_Display hex_digit_display_15 (.value(S1));  // open: dp
endmodule

module ALU (
  input  [3:0] A5,
  input  [3:0] A4,
  input  [3:0] A3,
  input  [3:0] A2,
  input  [3:0] A1,
  input  Sign_of_A,
  input  [3:0] B5,
  input  [3:0] B4,
  input  [3:0] B3,
  input  [3:0] B2,
  input  [3:0] B1,
  input  Sign_of_B,
  input  Operation,
  output [3:0] S5,
  output [3:0] S4,
  output [3:0] S3,
  output [3:0] S2,
  output [3:0] S1,
  output Sign
);

  wire n5_digit_comparator_1_out_11, n5_digit_comparator_1_out_13;
  wire [3:0] A1_B1, A1_B1_t, A2_B2, A2_B2_t, A3_B3, A3_B3_t, A4_B4, A4_B4_t, A5_B5, A5_B5_t;

  Multiplexer #(.select(3), .width(4), .enable("false")) multiplexer_1 (
    .in0(A1_B1), .in1(A1_B1_t), .in2(A1_B1_t), .in3(A1_B1), .in4(A1_B1_t), .in5(A1_B1), .in6(A1_B1),
    .in7(A1_B1_t), .out(S1), .sel({Sign_of_A, Sign_of_B, Operation}));
  _5_digit_BCD_subtractor u_5_digit_bcd_subtractor_1 (
    .A4(A4), .A3(A3), .A2(A2), .A1(A1), .B4(B4), .B3(B3), .B2(B2), .B1(B1), .D1(A1_B1_t), .D2(A2_B2_t),
    .D3(A3_B3_t), .D4(A4_B4_t), .D5(A5_B5_t), .A5(A5), .B5(B5));  // open: Negative
  Multiplexer #(.select(3), .width(4), .enable("false")) multiplexer_2 (
    .in0(A2_B2), .in1(A2_B2_t), .in2(A2_B2_t), .in3(A2_B2), .in4(A2_B2_t), .in5(A2_B2), .in6(A2_B2),
    .in7(A2_B2_t), .out(S2), .sel({Sign_of_A, Sign_of_B, Operation}));
  _5_digit_BCD_adder u_5_digit_bcd_adder_1 (
    .A5(A5), .A4(A4), .A3(A3), .A2(A2), .A1(A1), .B5(B5), .B4(B4), .B3(B3), .B2(B2), .B1(B1), .D1(A1_B1),
    .D2(A2_B2), .D3(A3_B3), .D4(A4_B4), .D5(A5_B5));  // open: C
  Multiplexer #(.select(3), .width(4), .enable("false")) multiplexer_3 (
    .in0(A3_B3), .in1(A3_B3_t), .in2(A3_B3_t), .in3(A3_B3), .in4(A3_B3_t), .in5(A3_B3), .in6(A3_B3),
    .in7(A3_B3_t), .out(S3), .sel({Sign_of_A, Sign_of_B, Operation}));
  _5_digit_Comparator u_5_digit_comparator_1 (
    .out_13(n5_digit_comparator_1_out_13), .out_11(n5_digit_comparator_1_out_11), .A5(A5), .A4(A4), .A3(A3),
    .A2(A2), .A1(A1), .B5(B5), .B4(B4), .B3(B3), .B2(B2), .B1(B1));  // open: out_12
  Multiplexer #(.select(3), .width(4), .enable("false")) multiplexer_4 (
    .in0(A4_B4), .in1(A4_B4_t), .in2(A4_B4_t), .in3(A4_B4), .in4(A4_B4_t), .in5(A4_B4), .in6(A4_B4),
    .in7(A4_B4_t), .out(S4), .sel({Sign_of_A, Sign_of_B, Operation}));
  Multiplexer #(.select(3), .enable("false")) multiplexer_5 (
    .in0(1'b0), .in1(n5_digit_comparator_1_out_13), .in2(n5_digit_comparator_1_out_13), .in3(1'b0),
    .in4(n5_digit_comparator_1_out_11), .in5(1'b1), .in6(1'b1), .in7(n5_digit_comparator_1_out_11),
    .out(Sign), .sel({Sign_of_A, Sign_of_B, Operation}));
  Multiplexer #(.select(3), .width(4), .enable("false")) multiplexer_6 (
    .in0(A5_B5), .in1(A5_B5_t), .in2(A5_B5_t), .in3(A5_B5), .in4(A5_B5_t), .in5(A5_B5), .in6(A5_B5),
    .in7(A5_B5_t), .out(S5), .sel({Sign_of_A, Sign_of_B, Operation}));

  // Other names for the same wires on the sheet: Op = Operation; B = Sign_of_B; A = Sign_of_A

  // Notes on the sheet:
  //   S1
  //   S2
  //   S3
  //   S4
  //   S5
endmodule

// +
module _5_digit_BCD_adder (
  input  [3:0] A5,
  input  [3:0] A4,
  input  [3:0] A3,
  input  [3:0] A2,
  input  [3:0] A1,
  input  [3:0] B5,
  input  [3:0] B4,
  input  [3:0] B3,
  input  [3:0] B2,
  input  [3:0] B1,
  output [3:0] D1,
  output [3:0] D2,
  output [3:0] D3,
  output [3:0] D4,
  output [3:0] D5,
  output C
);

  wire n4_bit_bcd_adder_1_c_out, n4_bit_bcd_adder_2_c_out, n4_bit_bcd_adder_3_c_out, n4_bit_bcd_adder_4_c_out;

  _4_bit_BCD_Adder u_4_bit_bcd_adder_1 (.A(A1), .B(B1), .S(D1), .c_out(n4_bit_bcd_adder_1_c_out));  // open: c_in
  _4_bit_BCD_Adder u_4_bit_bcd_adder_2 (
    .A(A2), .B(B2), .S(D2), .c_in(n4_bit_bcd_adder_1_c_out), .c_out(n4_bit_bcd_adder_2_c_out));
  _4_bit_BCD_Adder u_4_bit_bcd_adder_3 (
    .A(A3), .B(B3), .S(D3), .c_in(n4_bit_bcd_adder_2_c_out), .c_out(n4_bit_bcd_adder_3_c_out));
  _4_bit_BCD_Adder u_4_bit_bcd_adder_4 (
    .A(A4), .B(B4), .S(D4), .c_in(n4_bit_bcd_adder_3_c_out), .c_out(n4_bit_bcd_adder_4_c_out));
  _4_bit_BCD_Adder u_4_bit_bcd_adder_5 (.A(A5), .B(B5), .S(D5), .c_in(n4_bit_bcd_adder_4_c_out), .c_out(C));
  Hex_Digit_Display hex_digit_display_1 (.value(A4));  // open: dp
  Hex_Digit_Display hex_digit_display_2 (.value(A5));  // open: dp
  Hex_Digit_Display hex_digit_display_3 (.value(B5));  // open: dp
  Hex_Digit_Display hex_digit_display_4 (.value(B4));  // open: dp
  Hex_Digit_Display hex_digit_display_5 (.value({3'b000, C}));  // open: dp
  Hex_Digit_Display hex_digit_display_6 (.value(D5));  // open: dp
  Hex_Digit_Display hex_digit_display_7 (.value(A3));  // open: dp
  Hex_Digit_Display hex_digit_display_8 (.value(A2));  // open: dp
  Hex_Digit_Display hex_digit_display_9 (.value(B2));  // open: dp
  Hex_Digit_Display hex_digit_display_10 (.value(B3));  // open: dp
  Hex_Digit_Display hex_digit_display_11 (.value(D3));  // open: dp
  Hex_Digit_Display hex_digit_display_12 (.value(D4));  // open: dp
  Hex_Digit_Display hex_digit_display_13 (.value(A1));  // open: dp
  Hex_Digit_Display hex_digit_display_14 (.value(B1));  // open: dp
  Hex_Digit_Display hex_digit_display_15 (.value(D2));  // open: dp
  Hex_Digit_Display hex_digit_display_16 (.value(D1));  // open: dp

  // Other names for the same wires on the sheet: C_t[0] = C; S1[3:0] = D1; S2[3:0] = D2; S3[3:0] = D3; S4[3:0] = D4;
  //   S5[3:0] = D5

  // Notes on the sheet:
  //   +
  //   _______
endmodule

// -
module _5_digit_BCD_subtractor (
  input  [3:0] A5,
  input  [3:0] A4,
  input  [3:0] A3,
  input  [3:0] A2,
  input  [3:0] A1,
  input  [3:0] B5,
  input  [3:0] B4,
  input  [3:0] B3,
  input  [3:0] B2,
  input  [3:0] B1,
  output [3:0] D1,
  output [3:0] D2,
  output [3:0] D3,
  output [3:0] D4,
  output [3:0] D5,
  output Negative
);

  wire sign_bit_1_out_2, sign_bit_1_out_3, sign_bit_1_out_4, sign_bit_1_out_5, sign_bit_1_out_6,
       sign_bit_1_out_7, sign_bit_1_out_8, sign_bit_1_out_9;
  wire [3:0] A_prime_1, A_prime_2, A_prime_3, A_prime_4, A_prime_5, B_prime_1, B_prime_2, B_prime_3,
       B_prime_4, B_prime_5, n4_bit_bcd_9_s_complementer_1_out_2, n4_bit_bcd_9_s_complementer_2_out_2,
       n4_bit_bcd_9_s_complementer_3_out_2, n4_bit_bcd_9_s_complementer_4_out_2,
       n4_bit_bcd_9_s_complementer_5_out_2, n5_digit_bcd_adder_1_d1, n5_digit_bcd_adder_1_d2,
       n5_digit_bcd_adder_1_d3, n5_digit_bcd_adder_1_d4, n5_digit_bcd_adder_1_d5;

  _4_bit_BCD_9_s_Complementer u_4_bit_bcd_9_s_complementer_1 (
    .in_1(B_prime_5), .out_2(n4_bit_bcd_9_s_complementer_1_out_2));
  _4_bit_BCD_9_s_Complementer u_4_bit_bcd_9_s_complementer_2 (
    .in_1(B_prime_4), .out_2(n4_bit_bcd_9_s_complementer_2_out_2));
  _5_digit_BCD_adder u_5_digit_bcd_adder_1 (
    .A5(A_prime_5), .A4(A_prime_4), .A3(A_prime_3), .A2(A_prime_2), .A1(A_prime_1),
    .B5(n4_bit_bcd_9_s_complementer_1_out_2), .B4(n4_bit_bcd_9_s_complementer_2_out_2),
    .B3(n4_bit_bcd_9_s_complementer_4_out_2), .B2(n4_bit_bcd_9_s_complementer_5_out_2),
    .B1(n4_bit_bcd_9_s_complementer_3_out_2), .D1(n5_digit_bcd_adder_1_d1), .D2(n5_digit_bcd_adder_1_d2),
    .D3(n5_digit_bcd_adder_1_d3), .D4(n5_digit_bcd_adder_1_d4), .D5(n5_digit_bcd_adder_1_d5));  // open: C
  _4_bit_BCD_9_s_Complementer u_4_bit_bcd_9_s_complementer_3 (
    .in_1(B_prime_1), .out_2(n4_bit_bcd_9_s_complementer_3_out_2));
  _4_bit_BCD_9_s_Complementer u_4_bit_bcd_9_s_complementer_4 (
    .in_1(B_prime_3), .out_2(n4_bit_bcd_9_s_complementer_4_out_2));
  _4_bit_BCD_9_s_Complementer u_4_bit_bcd_9_s_complementer_5 (
    .in_1(B_prime_2), .out_2(n4_bit_bcd_9_s_complementer_5_out_2));
  _5_digit_BCD_adder u_5_digit_bcd_adder_2 (
    .A5(n5_digit_bcd_adder_1_d5), .A4(n5_digit_bcd_adder_1_d4), .A3(n5_digit_bcd_adder_1_d3),
    .A2(n5_digit_bcd_adder_1_d2), .A1(n5_digit_bcd_adder_1_d1), .B5(4'b0000), .B4(4'b0000), .B3(4'b0000),
    .B2(4'b0000), .B1(4'b0001), .D1(D1), .D2(D2), .D3(D3), .D4(D4), .D5(D5));  // open: C
  _5_digit_Comparator u_5_digit_comparator_1 (
    .out_13(Negative), .A5(A5), .A4(A4), .A3(A3), .A2(A2), .A1(A1), .B5(B5), .B4(B4), .B3(B3), .B2(B2),
    .B1(B1));  // open: out_11, out_12
  Twister twister_1 (.A(A5), .In(Negative), .B(B5), .A_prime(A_prime_5), .B_prime(B_prime_5));
  Twister twister_2 (.A(A4), .In(Negative), .B(B4), .A_prime(A_prime_4), .B_prime(B_prime_4));
  Twister twister_3 (.A(A3), .In(Negative), .B(B3), .A_prime(A_prime_3), .B_prime(B_prime_3));
  Twister twister_4 (.A(A2), .In(Negative), .B(B2), .A_prime(A_prime_2), .B_prime(B_prime_2));
  Twister twister_5 (.A(A1), .In(Negative), .B(B1), .A_prime(A_prime_1), .B_prime(B_prime_1));
  _7_Segment_Display u_7_segment_display_1 (
    .g(sign_bit_1_out_2), .f(sign_bit_1_out_3), .a(sign_bit_1_out_4), .b(sign_bit_1_out_5),
    .e(sign_bit_1_out_6), .d(sign_bit_1_out_7), .c(sign_bit_1_out_8), .dp(sign_bit_1_out_9));
  Sign_Bit sign_bit_1 (
    .out_2(sign_bit_1_out_2), .out_3(sign_bit_1_out_3), .out_4(sign_bit_1_out_4), .out_5(sign_bit_1_out_5),
    .out_6(sign_bit_1_out_6), .out_7(sign_bit_1_out_7), .out_8(sign_bit_1_out_8), .out_9(sign_bit_1_out_9),
    .in_1(Negative));
  Hex_Digit_Display hex_digit_display_1 (.value(A4));  // open: dp
  Hex_Digit_Display hex_digit_display_2 (.value(A5));  // open: dp
  Hex_Digit_Display hex_digit_display_3 (.value(B4));  // open: dp
  Hex_Digit_Display hex_digit_display_4 (.value(B5));  // open: dp
  Hex_Digit_Display hex_digit_display_5 (.value(D5));  // open: dp
  Hex_Digit_Display hex_digit_display_6 (.value(D4));  // open: dp
  Hex_Digit_Display hex_digit_display_7 (.value(A3));  // open: dp
  Hex_Digit_Display hex_digit_display_8 (.value(A2));  // open: dp
  Hex_Digit_Display hex_digit_display_9 (.value(B2));  // open: dp
  Hex_Digit_Display hex_digit_display_10 (.value(B3));  // open: dp
  Hex_Digit_Display hex_digit_display_11 (.value(D3));  // open: dp
  Hex_Digit_Display hex_digit_display_12 (.value(D2));  // open: dp
  Hex_Digit_Display hex_digit_display_13 (.value(A1));  // open: dp
  Hex_Digit_Display hex_digit_display_14 (.value(B1));  // open: dp
  Hex_Digit_Display hex_digit_display_15 (.value(D1));  // open: dp

  // Other names for the same wires on the sheet: S1[3:0] = D1; S2[3:0] = D2; S3[3:0] = D3; S4[3:0] = D4; S5[3:0] = D5

  // Notes on the sheet:
  //   -
  //   _______
endmodule

// ?
module _5_digit_Comparator (
  input  [3:0] A5,
  input  [3:0] A4,
  input  [3:0] A3,
  input  [3:0] A2,
  input  [3:0] A1,
  input  [3:0] B5,
  input  [3:0] B4,
  input  [3:0] B3,
  input  [3:0] B2,
  input  [3:0] B1,
  output out_11,
  output out_12,
  output out_13
);

  wire and_1_out, and_2_out, and_3_out, and_4_out, n4_bit_comparator_1_out_3, n4_bit_comparator_1_out_4,
       n4_bit_comparator_1_out_5, n4_bit_comparator_2_out_3, n4_bit_comparator_2_out_4,
       n4_bit_comparator_2_out_5, n4_bit_comparator_3_out_3, n4_bit_comparator_3_out_4,
       n4_bit_comparator_3_out_5, n4_bit_comparator_4_out_3, n4_bit_comparator_4_out_4,
       n4_bit_comparator_4_out_5, n4_bit_comparator_5_out_3, n4_bit_comparator_5_out_4, not_1_out, not_2_out,
       not_3_out, not_4_out;

  _4_bit_Comparator u_4_bit_comparator_1 (
    .out_5(n4_bit_comparator_1_out_5), .A(A5), .B(B5), .out_3(n4_bit_comparator_1_out_3),
    .out_4(n4_bit_comparator_1_out_4));
  not not_1 (not_1_out, n4_bit_comparator_1_out_5);
  _4_bit_Comparator u_4_bit_comparator_2 (
    .out_5(n4_bit_comparator_2_out_5), .A(A4), .B(B4), .out_3(n4_bit_comparator_2_out_3),
    .out_4(n4_bit_comparator_2_out_4));
  not not_2 (not_2_out, n4_bit_comparator_2_out_5);
  _4_bit_Comparator u_4_bit_comparator_3 (
    .out_5(n4_bit_comparator_3_out_5), .A(A3), .B(B3), .out_3(n4_bit_comparator_3_out_3),
    .out_4(n4_bit_comparator_3_out_4));
  not not_3 (not_3_out, n4_bit_comparator_3_out_5);
  _4_bit_Comparator u_4_bit_comparator_4 (
    .out_5(n4_bit_comparator_4_out_5), .A(A2), .B(B2), .out_3(n4_bit_comparator_4_out_3),
    .out_4(n4_bit_comparator_4_out_4));
  not not_4 (not_4_out, n4_bit_comparator_4_out_5);
  _4_bit_Comparator u_4_bit_comparator_5 (
    .A(A1), .B(B1), .out_3(n4_bit_comparator_5_out_3), .out_4(n4_bit_comparator_5_out_4));  // open: out_5
  and and_1 (and_1_out, not_1_out, n4_bit_comparator_2_out_3);
  and and_2 (and_2_out, not_2_out, not_1_out, n4_bit_comparator_3_out_3);
  and and_3 (and_3_out, not_1_out, not_3_out, n4_bit_comparator_4_out_3, not_2_out);
  and and_4 (and_4_out, not_1_out, not_4_out, not_2_out, not_3_out, n4_bit_comparator_5_out_3);
  and and_5 (out_12, n4_bit_comparator_1_out_4, n4_bit_comparator_2_out_4, n4_bit_comparator_5_out_4, n4_bit_comparator_3_out_4, n4_bit_comparator_4_out_4);
  or or_1 (out_11, n4_bit_comparator_1_out_3, and_1_out, and_2_out, and_3_out, and_4_out);
  Hex_Digit_Display hex_digit_display_1 (.value(A5));  // open: dp
  Hex_Digit_Display hex_digit_display_2 (.value(A4));  // open: dp
  Hex_Digit_Display hex_digit_display_3 (.value(B5));  // open: dp
  Hex_Digit_Display hex_digit_display_4 (.value(B4));  // open: dp
  Hex_Digit_Display hex_digit_display_5 (.value(A3));  // open: dp
  Hex_Digit_Display hex_digit_display_6 (.value(A2));  // open: dp
  Hex_Digit_Display hex_digit_display_7 (.value(B3));  // open: dp
  Hex_Digit_Display hex_digit_display_8 (.value(B2));  // open: dp
  nor nor_1 (out_13, out_12, out_11);
  Hex_Digit_Display hex_digit_display_9 (.value(A1));  // open: dp
  Hex_Digit_Display hex_digit_display_10 (.value(B1));  // open: dp

  // Other names for the same wires on the sheet: tunnel = out_12; tunnel_t = out_11
endmodule

module _4_bit_Comparator (
  input  [3:0] A,
  input  [3:0] B,
  output out_3,
  output out_4,
  output out_5
);

  wire _0, _1, _2, _3, and_2_out, and_3_out, and_4_out, and_5_out;

  xnor xnor_1 (_0, A[0], B[0]);
  xnor xnor_2 (_1, A[1], B[1]);
  xnor xnor_3 (_2, A[2], B[2]);
  and and_1 (out_4, _0, _1, _2, _3);
  xnor xnor_4 (_3, A[3], B[3]);
  nor nor_1 (out_5, out_4, out_3);
  and and_2 (and_2_out, A[0], _1, _3, _2, ~B[0]);  // AND_Gate
  and and_3 (and_3_out, A[1], _3, _2, ~B[1]);  // AND_Gate
  and and_4 (and_4_out, A[2], _3, ~B[2]);  // AND_Gate
  and and_5 (and_5_out, A[3], ~B[3]);  // AND_Gate
  or or_1 (out_3, and_2_out, and_3_out, and_4_out, and_5_out);

  // Other names for the same wires on the sheet: tunnel = out_4; tunnel_t = out_3

  // Notes on the sheet:
  //   INPUT
  //   EQUIVALENCE
  //   A    B
  //   OUTPUT
  //   A > B
endmodule

module _4_bit_BCD_Adder (
  input  c_in,
  input  [3:0] A,
  input  [3:0] B,
  output [3:0] S,
  output c_out
);

  wire adder_1_cout, adder_2_cout, n4_bit_comparator_1_out_3;
  wire [2:2] or_1_out;
  wire [3:0] adder_1_out;

  Hex_Digit_Display hex_digit_display_1 (.value(A));  // open: dp
  Adder #(.width(4)) adder_1 (.a(A), .b(B), .out(adder_1_out), .cin(c_in), .cout(adder_1_cout));
  Hex_Digit_Display hex_digit_display_2 (.value(B));  // open: dp
  _4_bit_Comparator u_4_bit_comparator_1 (
    .A(adder_1_out), .B(4'b1001), .out_3(n4_bit_comparator_1_out_3));  // open: out_5, out_4
  or or_1 (or_1_out[2], n4_bit_comparator_1_out_3, adder_1_cout);
  Hex_Digit_Display hex_digit_display_3 (.value(S));  // open: dp
  Hex_Digit_Display hex_digit_display_4 (.value({3'b000, c_out}));  // open: dp
  Adder #(.width(4)) adder_2 (
    .a(adder_1_out), .b({1'b0, {2{or_1_out[2]}}, 1'b0}), .out(S), .cout(adder_2_cout));  // open: cin
  or or_2 (c_out, adder_2_cout, adder_1_cout);

  // Other names for the same wires on the sheet: C[0] = c_out

  // Notes on the sheet:
  //   +
  //   =
endmodule

module _4_bit_BCD_9_s_Complementer (
  input  [3:0] in_1,
  output [3:0] out_2
);

  Hex_Digit_Display hex_digit_display_1 (.value(in_1));  // open: dp
  Hex_Digit_Display hex_digit_display_2 (.value(out_2));  // open: dp
  Subtractor #(.width(4)) subtractor_1 (.a(4'b1001), .b(in_1), .out(out_2));  // open: bin, bout

  // Notes on the sheet:
  //   =>
endmodule

// Twist
module Twister (
  input  [3:0] A,
  input  In,
  input  [3:0] B,
  output [3:0] A_prime,
  output [3:0] B_prime
);

  Multiplexer #(.width(4), .enable("false")) multiplexer_1 (.in0(A), .in1(B), .out(A_prime), .sel(In));
  Multiplexer #(.width(4), .enable("false")) multiplexer_2 (.in0(B), .in1(A), .out(B_prime), .sel(In));
endmodule

module Sign_Bit (
  input  in_1,
  output out_2,
  output out_3,
  output out_4,
  output out_5,
  output out_6,
  output out_7,
  output out_8,
  output out_9
);

  Multiplexer #(.width(8), .enable("false")) multiplexer_1 (
    .in0(8'h7e), .in1(8'h1), .out({out_9, out_8, out_7, out_6, out_5, out_4, out_3, out_2}), .sel(in_1));
  _7_Segment_Display u_7_segment_display_1 (
    .g(out_2), .f(out_3), .a(out_4), .b(out_5), .e(out_6), .d(out_7), .c(out_8), .dp(out_9));
endmodule

module Operator_Bit (
  input  EN,
  input  in_2,
  output out_3,
  output out_4,
  output out_5,
  output out_6,
  output out_7,
  output out_8,
  output out_9,
  output out_10
);

  Multiplexer #(.width(8)) multiplexer_1 (
    .in0(8'h49), .in1(8'h1), .out({out_10, out_9, out_8, out_7, out_6, out_5, out_4, out_3}), .sel(in_2),
    .en(EN));
  _7_Segment_Display u_7_segment_display_1 (
    .g(out_3), .f(out_4), .a(out_5), .b(out_6), .e(out_7), .d(out_8), .c(out_9), .dp(out_10));
endmodule
