// Logisim project Digital Lock.circ as structural Verilog: 3 circuits, main circuit main
module main (
);

  wire _00, _01, _02, _03, _04, _10, _11, _12, _13, _14, _20, _21, _22, _23, _24, _30, _31, _32, _33, _34,
       _40, _41, _42, _43, _44, AdMd, Admin_Mode, and_1_out, and_2_out, and_3_out, and_4_out, and_6_out,
       and_7_out, Clear, Lock, M00, M01, M02, M03, M04, M10, M11, M12, M13, M14, M20, M21, M22, M23, M24,
       M30, M31, M32, M33, M34, M40, M41, M42, M43, M44, matcher_1_out_13, matcher_2_out_14, Open, or_1_out,
       or_2_out, or_3_out, or_4_out, Reboot, Reset_Lock, ResetOK, Set, Set_Master_Pass;

  Button _0 (.out(_00));
  Button _5 (.out(_10));
  Button u__10 (.out(_20));
  Button _15 (.out(_30));
  Button u__20 (.out(_40));
  Button O (.out(Open));
  Button S (.out(Set));
  Button _0_1 (.out(Reboot));
  DotMatrix #(.inputtype("row"), .matrixrows(5)) dotmatrix_1 (
    .row0({M00, M01, M02, M03, M04}), .row1({M10, M11, M12, M13, M14}), .row2({M20, M21, M22, M23, M24}),
    .row3({M30, M31, M32, M33, M34}), .row4({M40, M41, M42, M43, M44}));
  Button _1 (.out(_01));
  Button _6 (.out(_11));
  Button u__11 (.out(_21));
  Button _16 (.out(_31));
  Button u__21 (.out(_41));
  Button C (.out(Clear));
  Button S_2 (.out(Set_Master_Pass));
  Button _0_2 (.out(Reset_Lock));
  Button _2 (.out(_02));
  Button _3 (.out(_03));
  Button _8 (.out(_13));
  Button _7 (.out(_12));
  Button u__12 (.out(_22));
  Button u__13 (.out(_23));
  Button _17 (.out(_32));
  Button _18 (.out(_33));
  Button u__22 (.out(_42));
  Button u__23 (.out(_43));
  Button A (.out(Admin_Mode));
  LED led_1 (.in(Lock));
  Button _4 (.out(_04));
  Button _9 (.out(_14));
  Button u__14 (.out(_24));
  Button _19 (.out(_34));
  Button u__24 (.out(_44));
  LED led_2 (.in(AdMd));
  and and_1 (and_1_out, AdMd, Set);
  J_K_Flip_Flop j_k_ff_1 (.J(_00), .clk(_00), .K(_00), .Q(M00), .reset(or_4_out));  // open: Qn, preset, en
  J_K_Flip_Flop j_k_ff_2 (.J(_10), .clk(_10), .K(_10), .Q(M10), .reset(or_4_out));  // open: Qn, preset, en
  J_K_Flip_Flop j_k_ff_3 (.J(_20), .clk(_20), .K(_20), .Q(M20), .reset(or_4_out));  // open: Qn, preset, en
  J_K_Flip_Flop j_k_ff_4 (.J(_30), .clk(_30), .K(_30), .Q(M30), .reset(or_4_out));  // open: Qn, preset, en
  J_K_Flip_Flop j_k_ff_5 (.J(_40), .clk(_40), .K(_40), .Q(M40), .reset(or_4_out));  // open: Qn, preset, en
  and and_2 (and_2_out, AdMd, Set_Master_Pass);
  J_K_Flip_Flop j_k_ff_6 (.J(_01), .clk(_01), .K(_01), .Q(M01), .reset(or_4_out));  // open: Qn, preset, en
  J_K_Flip_Flop j_k_ff_7 (.J(_11), .clk(_11), .K(_11), .Q(M11), .reset(or_4_out));  // open: Qn, preset, en
  J_K_Flip_Flop j_k_ff_8 (.J(_21), .clk(_21), .K(_21), .Q(M21), .reset(or_4_out));  // open: Qn, preset, en
  J_K_Flip_Flop j_k_ff_9 (.J(_31), .clk(_31), .K(_31), .Q(M31), .reset(or_4_out));  // open: Qn, preset, en
  J_K_Flip_Flop j_k_ff_10 (.J(_41), .clk(_41), .K(_41), .Q(M41), .reset(or_4_out));  // open: Qn, preset, en
  J_K_Flip_Flop j_k_ff_11 (.J(_02), .clk(_02), .K(_02), .Q(M02), .reset(or_4_out));  // open: Qn, preset, en
  J_K_Flip_Flop j_k_ff_12 (.J(_12), .clk(_12), .K(_12), .Q(M12), .reset(or_4_out));  // open: Qn, preset, en
  J_K_Flip_Flop j_k_ff_13 (.J(_22), .clk(_22), .K(_22), .Q(M22), .reset(or_4_out));  // open: Qn, preset, en
  J_K_Flip_Flop j_k_ff_14 (.J(_32), .clk(_32), .K(_32), .Q(M32), .reset(or_4_out));  // open: Qn, preset, en
  J_K_Flip_Flop j_k_ff_15 (.J(_42), .clk(_42), .K(_42), .Q(M42), .reset(or_4_out));  // open: Qn, preset, en
  Matcher matcher_1 (
    .EN(and_2_out), ._0R1({M00, M01, M02, M03, M04}), ._0R2({M10, M11, M12, M13, M14}),
    ._0R3({M20, M21, M22, M23, M24}), ._0R4({M30, M31, M32, M33, M34}), ._0R5({M40, M41, M42, M43, M44}),
    .R1({M00, M01, M02, M03, M04}), .R2({M10, M11, M12, M13, M14}), .R3({M20, M21, M22, M23, M24}),
    .R4({M30, M31, M32, M33, M34}), .R5({M40, M41, M42, M43, M44}), .out_13(matcher_1_out_13), .CLEAR(ResetOK));  // open: out_14
  Matcher matcher_2 (
    .EN(and_1_out), ._0R1({M00, M01, M02, M03, M04}), ._0R2({M10, M11, M12, M13, M14}),
    ._0R3({M20, M21, M22, M23, M24}), ._0R4({M30, M31, M32, M33, M34}), ._0R5({M40, M41, M42, M43, M44}),
    .R1({M00, M01, M02, M03, M04}), .R2({M10, M11, M12, M13, M14}), .R3({M20, M21, M22, M23, M24}),
    .R4({M30, M31, M32, M33, M34}), .R5({M40, M41, M42, M43, M44}), .CLEAR(ResetOK), .out_14(matcher_2_out_14));  // open: out_13
  J_K_Flip_Flop j_k_ff_16 (.J(_03), .clk(_03), .K(_03), .Q(M03), .reset(or_4_out));  // open: Qn, preset, en
  J_K_Flip_Flop j_k_ff_17 (.J(_13), .clk(_13), .K(_13), .Q(M13), .reset(or_4_out));  // open: Qn, preset, en
  J_K_Flip_Flop j_k_ff_18 (.J(_23), .clk(_23), .K(_23), .Q(M23), .reset(or_4_out));  // open: Qn, preset, en
  J_K_Flip_Flop j_k_ff_19 (.J(_33), .clk(_33), .K(_33), .Q(M33), .reset(or_4_out));  // open: Qn, preset, en
  J_K_Flip_Flop j_k_ff_20 (.J(_43), .clk(_43), .K(_43), .Q(M43), .reset(or_4_out));  // open: Qn, preset, en
  and and_3 (and_3_out, AdMd, Admin_Mode);
  and and_4 (and_4_out, Admin_Mode, matcher_1_out_13);
  and and_5 (ResetOK, Reset_Lock, AdMd);
  and and_6 (and_6_out, Lock, Open);
  and and_7 (and_7_out, Open, matcher_2_out_14);
  J_K_Flip_Flop j_k_ff_21 (.J(_04), .clk(_04), .K(_04), .Q(M04), .reset(or_4_out));  // open: Qn, preset, en
  J_K_Flip_Flop j_k_ff_22 (.J(_14), .clk(_14), .K(_14), .Q(M14), .reset(or_4_out));  // open: Qn, preset, en
  J_K_Flip_Flop j_k_ff_23 (.J(_24), .clk(_24), .K(_24), .Q(M24), .reset(or_4_out));  // open: Qn, preset, en
  J_K_Flip_Flop j_k_ff_24 (.J(_34), .clk(_34), .K(_34), .Q(M34), .reset(or_4_out));  // open: Qn, preset, en
  J_K_Flip_Flop j_k_ff_25 (.J(_44), .clk(_44), .K(_44), .Q(M44), .reset(or_4_out));  // open: Qn, preset, en
  or or_1 (or_1_out, and_3_out, and_4_out);
  or or_2 (or_2_out, ResetOK, Reboot);
  or or_3 (or_3_out, and_6_out, and_7_out);
  or or_4 (or_4_out, Clear, ResetOK, Reboot);
  J_K_Flip_Flop u_Admin_Mode (
    .J(or_1_out), .clk(or_1_out), .K(or_1_out), .Q(AdMd), .reset(or_2_out));  // open: Qn, preset, en
  J_K_Flip_Flop u_Lock (
    .J(or_3_out), .clk(or_3_out), .K(or_3_out), .Q(Lock), .reset(or_2_out));  // open: Qn, preset, en

  // Other names for the same wires on the sheet: R0[4:0] = {M00, M01, M02, M03, M04};
  //   R1[4:0] = {M10, M11, M12, M13, M14}; R2[4:0] = {M20, M21, M22, M23, M24}; R3[4:0] = {M30, M31, M32, M33, M34};
  //   R4[4:0] = {M40, M41, M42, M43, M44}
endmodule

module Matcher (
  input  [4:0] R1,
  input  [4:0] R2,
  input  [4:0] R3,
  input  [4:0] R4,
  input  [4:0] R5,
  input  CLEAR,
  input  EN,
  input  [4:0] _0R1,
  input  [4:0] _0R2,
  input  [4:0] _0R3,
  input  [4:0] _0R4,
  input  [4:0] _0R5,
  output out_13,
  output out_14
);

  wire comparator_1_eq, comparator_2_eq, comparator_3_eq, comparator_4_eq, comparator_5_eq;
  wire [4:0] register_1_q, register_2_q, register_3_q, register_4_q, register_5_q;

  Comparator #(.width(5)) comparator_1 (.a(R1), .b(register_1_q), .eq(comparator_1_eq));  // open: gt, lt
  Register #(.width(5)) register_1 (.D(_0R1), .Q(register_1_q), .clk(EN), .clr(CLEAR));  // open: en
  Register #(.width(5)) register_2 (.D(_0R2), .Q(register_2_q), .clk(EN), .clr(CLEAR));  // open: en
  Comparator #(.width(5)) comparator_2 (.a(R2), .b(register_2_q), .eq(comparator_2_eq));  // open: gt, lt
  and and_1 (out_13, comparator_1_eq, comparator_2_eq, comparator_3_eq, comparator_4_eq, comparator_5_eq);
  Register #(.width(5)) register_3 (.D(_0R3), .Q(register_3_q), .clk(EN), .clr(CLEAR));  // open: en
  Comparator #(.width(5)) comparator_3 (.a(R3), .b(register_3_q), .eq(comparator_3_eq));  // open: gt, lt
  Register #(.width(5)) register_4 (.D(_0R4), .Q(register_4_q), .clk(EN), .clr(CLEAR));  // open: en
  Comparator #(.width(5)) comparator_4 (.a(R4), .b(register_4_q), .eq(comparator_4_eq));  // open: gt, lt
  Register #(.width(5)) register_5 (.D(_0R5), .Q(register_5_q), .clk(EN), .clr(CLEAR));  // open: en
  Comparator #(.width(5)) comparator_5 (.a(R5), .b(register_5_q), .eq(comparator_5_eq));  // open: gt, lt

  assign out_14 = out_13;
endmodule

module test (
  input  in_1,
  input  [4:0] in_2
);

  wire matcher_1_p4;

  // Matcher matcher_1: pin names not known; wires that end beside it: in_2, in_2, in_2, matcher_1_p4
endmodule
