// Logisim project 7 Segment Display.circ as structural Verilog: 1 circuit, main circuit main
module main (
  input  [3:0] in_1
);

  wire and_1_out, P1_2_out, P1_out, P2_2_out, P2_3_out, P2_4_out, P2_out, P3_2_out, P3_3_out, P3_out,
       P4_2_out, P4_3_out, P4_out, P5_2_out, P5_3_out, P5_out, P6_2_out, P6_3_out, P6_4_out, P6_5_out,
       P6_out, P7_out, P8_out;

  and P2 (P2_out, ~in_1[1], ~in_1[0]);  // AND_Gate
  and P2_2 (P2_2_out, in_1[2], ~in_1[1]);  // AND_Gate
  and P2_3 (P2_3_out, in_1[2], ~in_1[0]);  // AND_Gate
  xor P1 (P1_out, in_1[2], in_1[1]);
  and and_1 (and_1_out, in_1[1], ~in_1[0]);  // AND_Gate
  and P5 (P5_out, in_1[1], ~in_1[0]);  // AND_Gate
  and P5_2 (P5_2_out, ~in_1[2], ~in_1[0]);  // AND_Gate
  and P6 (P6_out, in_1[1], ~in_1[0]);  // AND_Gate
  and P6_2 (P6_2_out, ~in_1[0], ~in_1[2]);  // AND_Gate
  and P6_3 (P6_3_out, in_1[2], ~in_1[1], in_1[0]);  // AND_Gate
  and P6_4 (P6_4_out, ~in_1[2], in_1[1]);  // AND_Gate
  or P2_4 (P2_4_out, P2_out, in_1[3], P2_2_out, P2_3_out);
  or P1_2 (P1_2_out, P1_out, and_1_out, in_1[3]);
  _7_Segment_Display u_7_segment_display_1 (
    .g(P1_2_out), .f(P2_4_out), .a(P3_out), .b(P4_out), .e(P5_3_out), .d(P6_5_out), .c(P7_out), .dp(P8_out));
  or P5_3 (P5_3_out, P5_out, P5_2_out);
  or P6_5 (P6_5_out, P6_out, P6_2_out, P6_3_out, in_1[3], P6_4_out);
  or P3 (P3_out, P3_2_out, in_1[3], in_1[1], P3_3_out);
  or P4 (P4_out, P4_2_out, ~in_1[2], P4_3_out);  // OR_Gate
  or P8 (P8_out, in_1[0], in_1[1], ~in_1[3], in_1[2], in_1[3]);  // OR_Gate
  or P7 (P7_out, in_1[0], ~in_1[1], in_1[2]);  // OR_Gate
  and P3_2 (P3_2_out, ~in_1[2], ~in_1[0]);  // AND_Gate
  and P3_3 (P3_3_out, in_1[2], in_1[0]);
  and P4_2 (P4_2_out, ~in_1[1], ~in_1[0]);  // AND_Gate
  and P4_3 (P4_3_out, in_1[1], in_1[0]);

  // Notes on the sheet:
  //   A
  //   B
  //   C
  //   D
  //   D
  //   C
  //   B
  //   A
endmodule
